# Fritzing sketch stepper (saved by Fritzing 0.9.6b)
breadboards: 1

parts:
  SM1 = 28BYJ-48 Stepper Motor [part_number=28BYJ-48]
  Driver1 = 28BYJ-48 Driver Module [part_number=ULN2003 package=THT]
  Microcontroller = Arduino Nano (Rev3.0)

nets:
  N1: SM1.blue-pin, Driver1.blue-pin
  N2: SM1.pink-pin, Driver1.pink-pin
  N3: SM1.yellow-pin, Driver1.yellow-pin
  N4: SM1.orange-pin, Driver1.orange-pin
  N5: SM1.red-pin, Driver1.red-pin
  N6: Driver1.IN1, Microcontroller.D11/MOSI
  N7: Driver1.IN2, Microcontroller.D10
  N8: Driver1.IN3, Microcontroller.D9
  N9: Driver1.IN4, Microcontroller.D8
  GND: Driver1.GND, Microcontroller.GND
  N10: Driver1.Vmotor, Microcontroller.5V

custom parts:
  28BYJ-48 Stepper Motor: Unipolar Stepper Motor 28BYJ-48 Top coil - pink & orange Bottom coil - blue & yellow Common rail - red Connector pins: blue - pink - yellow - orange - red
  28BYJ-48 Driver Module: ULN2003 Driver Module for the 28BYJ-48 Unipolar Stepper Motor LED A - Blue wire - Bottom coil left LED B - Pink wire - Top coil left LED C - Yellow wire - Bottom coil right LED D - Orange wire - Top coil right Common rail - red Connector pins: blue - pink - yellow - orange - red Control pins - IN1 to IN4 Power pins - GND & Vmotor (5-12V) On/Off jumper (if removed, power to motor is cut).
