# Fritzing sketch steppers (saved by Fritzing 0.9.6b)
breadboards: 1

parts:
  SM1 = 28BYJ-48 Stepper Motor [part_number=28BYJ-48]
  Driver1 = 28BYJ-48 Driver Module [part_number=ULN2003 package=THT]
  Microcontroller = Arduino Nano (Rev3.0)
  Driver2 = 28BYJ-48 Driver Module [part_number=ULN2003 package=THT]
  SM2 = 28BYJ-48 Stepper Motor [part_number=28BYJ-48]
  Power_plug2 = Power plug

nets:
  N1: SM1.blue-pin, Driver1.blue-pin
  N2: SM1.pink-pin, Driver1.pink-pin
  N3: SM1.yellow-pin, Driver1.yellow-pin
  N4: SM1.orange-pin, Driver1.orange-pin
  N5: SM1.red-pin, Driver1.red-pin
  N6: Driver1.IN1, Microcontroller.D7
  N7: Driver1.IN2, Microcontroller.D6
  N8: Driver1.IN3, Microcontroller.D5
  N9: Driver1.IN4, Microcontroller.D4
  GND: Driver1.GND, Microcontroller.GND, Driver2.GND, Power_plug2.GND
  5V: Driver1.Vmotor, Microcontroller.5V, Driver2.Vmotor, Power_plug2.VCC
  N10: Microcontroller.D8, Driver2.IN4
  N11: Microcontroller.D9, Driver2.IN3
  N12: Microcontroller.D10, Driver2.IN2
  N13: Microcontroller.D11/MOSI, Driver2.IN1
  N14: Driver2.blue-pin, SM2.blue-pin
  N15: Driver2.pink-pin, SM2.pink-pin
  N16: Driver2.yellow-pin, SM2.yellow-pin
  N17: Driver2.orange-pin, SM2.orange-pin
  N18: Driver2.red-pin, SM2.red-pin

notes:
  PowerBank
  5V

custom parts:
  28BYJ-48 Stepper Motor: Unipolar Stepper Motor 28BYJ-48 Top coil - pink & orange Bottom coil - blue & yellow Common rail - red Connector pins: blue - pink - yellow - orange - red
  28BYJ-48 Driver Module: ULN2003 Driver Module for the 28BYJ-48 Unipolar Stepper Motor LED A - Blue wire - Bottom coil left LED B - Pink wire - Top coil left LED C - Yellow wire - Bottom coil right LED D - Orange wire - Top coil right Common rail - red Connector pins: blue - pink - yellow - orange - red Control pins - IN1 to IN4 Power pins - GND & Vmotor (5-12V) On/Off jumper (if removed, power to motor is cut).
